# Fritzing sketch Wiring (saved by Fritzing 0.9.0b)
breadboards: 1

parts:
  R1 = Resistor [tolerance=±5% resistance=220 package=THT]
  R2 = Resistor [tolerance=±5% resistance=220 package=THT]
  LED1 = LED - 5mm [color="Red (633nm)" package="5 mm [THT]"]
  LED2 = LED - 5mm [color="Green (570nm)" package="5 mm [THT]"]
  J1 = female pin header, 5 pins [form="♀ (female)"]
  S1 = Pushbutton [package="[THT]"]
  R3 = Resistor [tolerance=±5% resistance=10k package=THT]
  Bauteil1 = Arduino Uno (Rev3)

nets:
  N1: R1.Pin_0, R2.Pin_0, J1.pin1, S1.Pin_1, S1.Pin_2, Bauteil1.GND
  N2: R1.Pin_1, LED1.cathode
  N3: R2.Pin_1, LED2.cathode
  N4: LED1.anode, Bauteil1.D8
  N5: LED2.anode, Bauteil1.D9_PWM
  N6: J1.pin3, Bauteil1.A5/SCL
  N7: J1.pin4, Bauteil1.A4/SDA
  N8: J1.pin5, R3.Pin_0, Bauteil1.5V
  N9: S1.Pin_3, S1.Pin_4, R3.Pin_1, Bauteil1.D7

notes:
  Connection to RPI
  pin
  5 4 3 2 1
